// Logisim project SEP architecture.circ as structural Verilog: 24 circuits, main circuit SEP Architecture
module SEP_Architecture (
  input  [7:0] Binary_Switches
);

  wire binary_keyboard_1_buffer_not_empty_indicator, clk, Clock_out, Enter_Button_out, HLT, IR, not_1_out,
       not_2_out, sep_cpu_1_memory_write_read_, sep_cpu_1_output_write;
  wire [3:0] binary_keyboard_1_keyboard_value, binary_keyboard_1_keyboard_value_2, ram_1_data, ram_1_data_2;
  wire [7:0] output_display_1_hundreds_digit, output_display_1_ones_digit, output_display_1_signe_digit,
       output_display_1_tens_digit, sep_cpu_1_memory_address_output, sep_cpu_1_memory_data_output,
       sep_cpu_1_output_port;

  SEP_CPU sep_cpu_1 (
    .Memory_Write_Read_(sep_cpu_1_memory_write_read_), .Output_Write(sep_cpu_1_output_write),
    .Input_Request(IR), .memory_data_input({ram_1_data_2, ram_1_data}),
    .input_port({binary_keyboard_1_keyboard_value_2, binary_keyboard_1_keyboard_value}),
    .memory_address_output(sep_cpu_1_memory_address_output),
    .memory_data_output(sep_cpu_1_memory_data_output), .output_port(sep_cpu_1_output_port), .clk(clk));
  Clock Clock (.out(Clock_out));
  and and_1 (clk, Clock_out, not_1_out);
  not not_1 (not_1_out, HLT);
  Output_Display output_display_1 (
    .\input (sep_cpu_1_output_port), .Ones_Digit(output_display_1_ones_digit),
    .Tens_Digit(output_display_1_tens_digit), .Hundreds_Digit(output_display_1_hundreds_digit),
    .Signe_Digit(output_display_1_signe_digit), .clk(clk), .output_write(sep_cpu_1_output_write));
  Hex_Digit_Display hex_digit_display_1 (.value(sep_cpu_1_output_port[7:4]));  // open: dp
  Hex_Digit_Display hex_digit_display_2 (.value(sep_cpu_1_output_port[3:0]));  // open: dp
  Hex_Digit_Display hex_digit_display_3 (.value(sep_cpu_1_memory_address_output[7:4]));  // open: dp
  Hex_Digit_Display hex_digit_display_4 (.value(sep_cpu_1_memory_address_output[3:0]));  // open: dp
  _7_Segment_Display u_7_segment_display_1 (
    .g(output_display_1_signe_digit[6]), .f(output_display_1_signe_digit[5]),
    .a(output_display_1_signe_digit[0]), .b(output_display_1_signe_digit[1]),
    .e(output_display_1_signe_digit[4]), .d(output_display_1_signe_digit[3]),
    .c(output_display_1_signe_digit[2]));  // open: dp
  Hex_Digit_Display hex_digit_display_5 (.value(sep_cpu_1_memory_data_output[7:4]));  // open: dp
  _7_Segment_Display u_7_segment_display_2 (
    .g(output_display_1_hundreds_digit[6]), .f(output_display_1_hundreds_digit[5]),
    .a(output_display_1_hundreds_digit[0]), .b(output_display_1_hundreds_digit[1]),
    .e(output_display_1_hundreds_digit[4]), .d(output_display_1_hundreds_digit[3]),
    .c(output_display_1_hundreds_digit[2]));  // open: dp
  not not_2 (not_2_out, sep_cpu_1_memory_write_read_);
  Hex_Digit_Display hex_digit_display_6 (.value(sep_cpu_1_memory_data_output[3:0]));  // open: dp
  Hex_Digit_Display hex_digit_display_7 (.value(ram_1_data_2));  // open: dp
  _7_Segment_Display u_7_segment_display_3 (
    .g(output_display_1_tens_digit[6]), .f(output_display_1_tens_digit[5]),
    .a(output_display_1_tens_digit[0]), .b(output_display_1_tens_digit[1]),
    .e(output_display_1_tens_digit[4]), .d(output_display_1_tens_digit[3]), .c(output_display_1_tens_digit[2]));  // open: dp
  RAM #(.bus("separate")) ram_1 (
    .addr(sep_cpu_1_memory_address_output), .din(sep_cpu_1_memory_data_output),
    .data({ram_1_data_2, ram_1_data}), .str(sep_cpu_1_memory_write_read_), .clk(clk), .ld(not_2_out));  // open: sel, clr
  Hex_Digit_Display hex_digit_display_8 (.value(ram_1_data));  // open: dp
  _7_Segment_Display u_7_segment_display_4 (
    .g(output_display_1_ones_digit[6]), .f(output_display_1_ones_digit[5]),
    .a(output_display_1_ones_digit[0]), .b(output_display_1_ones_digit[1]),
    .e(output_display_1_ones_digit[4]), .d(output_display_1_ones_digit[3]), .c(output_display_1_ones_digit[2]));  // open: dp
  Hex_Digit_Display hex_digit_display_9 (.value(binary_keyboard_1_keyboard_value_2));  // open: dp
  Binary_Keyboard binary_keyboard_1 (
    .Keyboard_Value({binary_keyboard_1_keyboard_value_2, binary_keyboard_1_keyboard_value}),
    .Binary_keyboard_input(Binary_Switches), .Enter_push_button(Enter_Button_out),
    .Buffer_not_empty_indicator(binary_keyboard_1_buffer_not_empty_indicator), .Input_Request(IR), .halt(HLT));
  Hex_Digit_Display hex_digit_display_10 (.value(binary_keyboard_1_keyboard_value));  // open: dp
  Hex_Digit_Display hex_digit_display_11 (.value(Binary_Switches[7:4]));  // open: dp
  Hex_Digit_Display hex_digit_display_12 (.value(Binary_Switches[3:0]));  // open: dp
  Button Enter_Button (.out(Enter_Button_out));
  LED Keyboard_Buffer_Loaded (.in(binary_keyboard_1_buffer_not_empty_indicator));

  // Notes on the sheet:
  //   already programmed (files with .RAM
  //   extension) and load it in the RAM. Or
  //   the same CPU definition found in the
  //   examples (files with .asm extensions),
  //   then you have to assemble it with
  //   format output, then copy it in the RAM.
  //   to this value manually before execution.
  //   To run a program on the architecture you
  //   have 2 options; choose one of the examples
  //   write your own program and assemble it
  //   with Customasm, you need though to use
  //   Customasm by choosing Logisim memory
  //   Generally the entry point for every program is
  //   different, then you should modify manually the
  //   PC accordingly, for instance, all examples begin
  //   execution at address 0x10, the PC should be put
  //   memory write/read_ signal
  //   output write signal
  //   input request signal
  //   output data bus
  //   Halt signal allows
  //   to stop the clock
  //   data from memory bus
  //   input keyboard bus
  //   address memory bus
  //   data to memory bus
  //   RAM
  //   256 Bytes
  //   Display
  //   The display is in signed decimal format
  //   The peers of 7 segments
  //   display attached to busses,
  //   are there only for debugging
  //   and monitoring purposes.
  //   Enter an 8 bits value to the keyboard
  //   by changing the switches and pushing
  //    Enter button, this value remains inside
  //   by INPUT instruction.
  //   the keyboard buffer until its consumption
endmodule

// SEP cpu
module SEP_CPU (
  input  clk,
  input  [7:0] memory_data_input,
  input  [7:0] input_port,
  output Memory_Write_Read_,
  output Output_Write,
  output Input_Request,
  output [7:0] memory_address_output,
  output [7:0] memory_data_output,
  output [7:0] output_port
);

  wire ABw, Accw, d_ff_1_q, d_ff_2_q, F0, F1, F2, IRw, M0, M1, PCw, SPw, zero;
  wire [7:0] acc_accumulator_1_output, ir_instruction_register_1_output, mux_4_1_8_bits_1_output,
       pc_program_counter_1_output, sp_stack_pointer_register_1_output;

  PC__Program_Counter pc_program_counter_1 (
    .\input (memory_data_output), .\output (pc_program_counter_1_output), .clk(clk), .write_enable(PCw));
  SP__Stack_Pointer_Register sp_stack_pointer_register_1 (
    .\input (memory_data_output), .\output (sp_stack_pointer_register_1_output), .clk(clk), .write_enable(SPw));
  Acc__Accumulator acc_accumulator_1 (
    .\input (memory_data_output), .\output (acc_accumulator_1_output), .clk(clk), .write_enable(Accw));
  Hex_Digit_Display hex_digit_display_1 (.value(memory_data_output[7:4]));  // open: dp
  D_Flip_Flop #(.trigger("high")) d_ff_1 (.clk(clk), .D(zero), .Q(d_ff_1_q), .en(F1));  // open: Qn, preset, reset
  D_Flip_Flop #(.trigger("high")) d_ff_2 (
    .clk(clk), .D(memory_data_output[7]), .Q(d_ff_2_q), .en(F1));  // open: Qn, preset, reset
  Hex_Digit_Display hex_digit_display_2 (.value(memory_data_output[3:0]));  // open: dp
  Hex_Digit_Display hex_digit_display_3 (.value(pc_program_counter_1_output[7:4]));  // open: dp
  Hex_Digit_Display hex_digit_display_4 (.value(sp_stack_pointer_register_1_output[7:4]));  // open: dp
  Hex_Digit_Display hex_digit_display_5 (.value(acc_accumulator_1_output[7:4]));  // open: dp
  CU__Control_Unit cu_control_unit_1 (
    .Accw(Accw), .SPw(SPw), .PCw(PCw), .IRw(IRw), .ABw(ABw), .F0(F0), .F1(F1), .F2(F2), .M0(M0), .M1(M1),
    .MWR_(Memory_Write_Read_), .OW(Output_Write), .IR(Input_Request), .ZF(d_ff_1_q), .NF(d_ff_2_q),
    .OP_code(ir_instruction_register_1_output), .clk(clk));
  Hex_Digit_Display hex_digit_display_6 (.value(pc_program_counter_1_output[3:0]));  // open: dp
  Hex_Digit_Display hex_digit_display_7 (.value(sp_stack_pointer_register_1_output[3:0]));  // open: dp
  Hex_Digit_Display hex_digit_display_8 (.value(acc_accumulator_1_output[3:0]));  // open: dp
  ALU__Arithmetic_and_Logic_Unit alu_arithmetic_and_logic_unit_1 (
    .A(acc_accumulator_1_output), .B(mux_4_1_8_bits_1_output), .S(memory_data_output), .zero(zero), .F2(F2),
    .F1(F1), .F0(F0));
  IR__Instruction_Register ir_instruction_register_1 (
    .\input (memory_data_input), .\output (ir_instruction_register_1_output), .clk(clk), .write_enable(IRw));
  Mux_4_1__8_bits mux_4_1_8_bits_1 (
    .Input_0(input_port), .Input_1(memory_data_input), .Input_2(pc_program_counter_1_output),
    .Input_3(sp_stack_pointer_register_1_output), .Output(mux_4_1_8_bits_1_output), .Select_1(M1),
    .Select_0(M0));
  Hex_Digit_Display hex_digit_display_9 (.value(mux_4_1_8_bits_1_output[7:4]));  // open: dp
  Hex_Digit_Display hex_digit_display_10 (.value(ir_instruction_register_1_output[3:0]));  // open: dp
  Hex_Digit_Display hex_digit_display_11 (.value(ir_instruction_register_1_output[7:4]));  // open: dp
  Hex_Digit_Display hex_digit_display_12 (.value(mux_4_1_8_bits_1_output[3:0]));  // open: dp
  LED IR (.in(Input_Request));
  LED u_M1 (.in(M1));
  LED OW (.in(Output_Write));
  LED MWR_ (.in(Memory_Write_Read_));
  Hex_Digit_Display hex_digit_display_13 (.value(memory_data_output[7:4]));  // open: dp
  LED u_M0 (.in(M0));
  LED u_F1 (.in(F1));
  LED u_F0 (.in(F0));
  LED u_F2 (.in(F2));
  Hex_Digit_Display hex_digit_display_14 (.value(memory_data_input[7:4]));  // open: dp
  Hex_Digit_Display hex_digit_display_15 (.value(memory_data_input[3:0]));  // open: dp
  Hex_Digit_Display hex_digit_display_16 (.value(input_port[7:4]));  // open: dp
  Hex_Digit_Display hex_digit_display_17 (.value(input_port[3:0]));  // open: dp
  Hex_Digit_Display hex_digit_display_18 (.value(memory_data_output[3:0]));  // open: dp
  LED u_ABw (.in(ABw));
  LED u_IRw (.in(IRw));
  LED u_PCw (.in(PCw));
  LED u_SPw (.in(SPw));
  AB__Address_Bus ab_address_bus_1 (
    .\input (memory_data_output), .\output (memory_address_output), .clk(clk), .write_enable(ABw));
  LED u_Accw (.in(Accw));
  Hex_Digit_Display hex_digit_display_19 (.value(memory_address_output[3:0]));  // open: dp
  Hex_Digit_Display hex_digit_display_20 (.value(memory_address_output[7:4]));  // open: dp

  assign output_port = memory_data_output;

  // Other names for the same wires on the sheet: IR = Input_Request; negative = memory_data_output[7];
  //   MWR_ = Memory_Write_Read_; OW = Output_Write

  // Notes on the sheet:
  //   shift).
  //   Note :
  //   F1 is the signal who enables
  //   the flags flip-flops, which
  //   means their modifications
  //   only occur for arithmetic
  //   operations (add,sub,nand,
  //   ZF
  //   NF
  //   0 : A
  //   1 : B
  //   3 : A-B
  //   5 : B-1
  //   ALU Functions :
  //   2 : A+B
  //   4 : B+1
  //   6 : A>>1 (shift right)
  //   7 : ~(A&B)  (nand)
endmodule

// CU
module CU__Control_Unit (
  input  clk,
  input  ZF,
  input  NF,
  input  [7:0] OP_code,
  output Accw,
  output SPw,
  output PCw,
  output IRw,
  output ABw,
  output F0,
  output F1,
  output F2,
  output M0,
  output M1,
  output MWR_,
  output OW,
  output IR
);

  wire not_1_out, sc_sequencer_controller_1_mux0, sc_sequencer_controller_1_mux1;
  wire [2:0] csr_control_signals_register_1_sc0;
  wire [7:0] csr_control_signals_register_1_j0, incrementation_8_bits_1_s,
       mpc_micro_instruction_program_counter_1_output, mux_4_1_8_bits_1_output;
  wire [23:0] rom_1_data;

  SC__Sequencer_Controller sc_sequencer_controller_1 (
    .sequencer_commands(csr_control_signals_register_1_sc0), .Mux1(sc_sequencer_controller_1_mux1),
    .Mux0(sc_sequencer_controller_1_mux0), .ZF(ZF), .NF(NF));
  Mux_4_1__8_bits mux_4_1_8_bits_1 (
    .Input_0(8'h1), .Input_1(OP_code), .Input_2(csr_control_signals_register_1_j0),
    .Input_3(incrementation_8_bits_1_s), .Output(mux_4_1_8_bits_1_output),
    .Select_1(sc_sequencer_controller_1_mux1), .Select_0(sc_sequencer_controller_1_mux0));
  Hex_Digit_Display hex_digit_display_1 (.value(mux_4_1_8_bits_1_output[7:4]));  // open: dp
  Hex_Digit_Display hex_digit_display_2 (.value(mux_4_1_8_bits_1_output[3:0]));  // open: dp
  Hex_Digit_Display hex_digit_display_3 (.value(csr_control_signals_register_1_j0[3:0]));  // open: dp
  Hex_Digit_Display hex_digit_display_4 (.value(csr_control_signals_register_1_j0[7:4]));  // open: dp
  MPC__Micro_instruction_Program_Counter mpc_micro_instruction_program_counter_1 (
    .clk(clk), .write_enable(1'b1), .\output (mpc_micro_instruction_program_counter_1_output),
    .\input (mux_4_1_8_bits_1_output));
  Incrementation__8_bits incrementation_8_bits_1 (
    .A(mpc_micro_instruction_program_counter_1_output), .S(incrementation_8_bits_1_s));
  Hex_Digit_Display hex_digit_display_5 (.value({1'b0, csr_control_signals_register_1_sc0}));  // open: dp
  Hex_Digit_Display hex_digit_display_6 (.value(mpc_micro_instruction_program_counter_1_output[7:4]));  // open: dp
  Hex_Digit_Display hex_digit_display_7 (.value(mpc_micro_instruction_program_counter_1_output[3:0]));  // open: dp
  not not_1 (not_1_out, clk);
  ROM #(.dataWidth(24)) rom_1 (.addr(mpc_micro_instruction_program_counter_1_output), .data(rom_1_data));  // open: sel
  CSR__Control_Signals_Register csr_control_signals_register_1 (
    .\input (rom_1_data), .clk(not_1_out), .write_enable(1'b1), .J7(csr_control_signals_register_1_j0[7]),
    .J6(csr_control_signals_register_1_j0[6]), .J5(csr_control_signals_register_1_j0[5]),
    .J4(csr_control_signals_register_1_j0[4]), .J3(csr_control_signals_register_1_j0[3]),
    .J2(csr_control_signals_register_1_j0[2]), .J1(csr_control_signals_register_1_j0[1]),
    .J0(csr_control_signals_register_1_j0[0]), .SC2(csr_control_signals_register_1_sc0[2]),
    .SC1(csr_control_signals_register_1_sc0[1]), .SC0(csr_control_signals_register_1_sc0[0]), .IR(IR),
    .OW(OW), .MWR_(MWR_), .M1(M1), .M0(M0), .F2(F2), .F1(F1), .F0(F0), .ABw(ABw), .IRw(IRw), .PCw(PCw),
    .SPw(SPw), .Accw(Accw));

  // Notes on the sheet:
  //   Sequencer Commands list :
  //   0 : increment address
  //   1 : jump address
  //   2 : jump to OPcode
  //   3 : jump to fetch address
  //   4 : jump address if ZF
  //   5 : jump address if not ZF
  //   6 : jump address if NF
  //   7 : jump address if not NF
  //   fetch address
  //   jump address
  //   sequencer commands
  //   MP ROM
  //   contents of rom_1 (hex, n*v repeats v):
  //   0 230 28c 4000 230 284 130 6121 230 284 6121 230 284 130 6400 230 284 130 6141 230 284 6141 230 284
  //   130 6161 230 284 6161 230 284 130 61e1 230 284 61e1 60c1 6000 230 6124 230 130 6124 284 330 620 3a2
  //   2a4 230 6124 382 330 6124 330 400 63a2 382 330 6121 230 284 130 6160 230 284 6160 44c000 6284 230
  //   6124 48e000 6284 230 6124 4c8000 6284 230 6124 50a000 6284 230 6124 6800 1000 6021 6002 6321
endmodule

// ALU
module ALU__Arithmetic_and_Logic_Unit (
  input  F2,
  input  F1,
  input  F0,
  input  [7:0] A,
  input  [7:0] B,
  output [7:0] S,
  output zero
);

  wire [7:0] adder_8_bits_1_s, decrementation_8_bits_1_s, incrementation_8_bits_1_s, nand_1_out,
       shift_right_1_s, subtractor_8_bits_1_s;

  Adder__8_bits adder_8_bits_1 (.A(A), .B(B), .S(adder_8_bits_1_s));  // open: Cout
  Subtractor__8_bits subtractor_8_bits_1 (.A(A), .B(B), .S(subtractor_8_bits_1_s));  // open: Cout
  Incrementation__8_bits incrementation_8_bits_1 (.A(B), .S(incrementation_8_bits_1_s));
  Decrementation__8_bits decrementation_8_bits_1 (.A(B), .S(decrementation_8_bits_1_s));
  Shift_Right shift_right_1 (.A(A), .S(shift_right_1_s));
  assign nand_1_out = ~(A & B);  // NAND_Gate nand_1, 8 bits wide
  Mux_8_1__8_bits mux_8_1_8_bits_1 (
    .Input_0(A), .Input_1(B), .Input_2(adder_8_bits_1_s), .Input_3(subtractor_8_bits_1_s),
    .Input_4(incrementation_8_bits_1_s), .Input_5(decrementation_8_bits_1_s), .Input_6(shift_right_1_s),
    .Input_7(nand_1_out), .Output(S), .Select_2(F2), .Select_1(F1), .Select_0(F0));
  nor nor_1 (zero, S[0], S[1], S[2], S[3], S[4], S[5], S[6], S[7]);

  // Notes on the sheet:
  //   Zero detector
endmodule

// Display
module Output_Display (
  input  clk,
  input  output_write,
  input  [7:0] \input ,
  output [7:0] Ones_Digit,
  output [7:0] Tens_Digit,
  output [7:0] Hundreds_Digit,
  output [7:0] Signe_Digit
);

  wire [2:0] output_register_1_output_2;
  wire [3:0] output_register_1_output;

  Output_Register output_register_1 (
    .\input (\input ), .\output ({Signe_Digit[6], output_register_1_output_2, output_register_1_output}),
    .clk(clk), .write_enable(output_write));
  Hex_Digit_Display hex_digit_display_1 (.value(output_register_1_output));  // open: dp
  Hex_Digit_Display hex_digit_display_2 (.value({Signe_Digit[6], output_register_1_output_2}));  // open: dp
  ROM rom_1 (
    .addr({Signe_Digit[6], output_register_1_output_2, output_register_1_output}), .data(Ones_Digit));  // open: sel
  ROM rom_2 (
    .addr({Signe_Digit[6], output_register_1_output_2, output_register_1_output}), .data(Tens_Digit));  // open: sel
  ROM rom_3 (
    .addr({Signe_Digit[6], output_register_1_output_2, output_register_1_output}), .data(Hundreds_Digit));  // open: sel

  assign {Signe_Digit[7], Signe_Digit[5:0]} = {7{1'b0}};

  // Notes on the sheet:
  //   Ones ROM
  //   Tens ROM
  //   Hundreds ROM
  //   contents of rom_1 (hex, n*v repeats v):
  //   3f 6 5b 4f 66 6d 7d 7 7f 6f 3f 6 5b 4f 66 6d 7d 7 7f 6f 3f 6 5b 4f 66 6d 7d 7 7f 6f 3f 6 5b 4f 66 6d
  //   7d 7 7f 6f 3f 6 5b 4f 66 6d 7d 7 7f 6f 3f 6 5b 4f 66 6d 7d 7 7f 6f 3f 6 5b 4f 66 6d 7d 7 7f 6f 3f 6
  //   5b 4f 66 6d 7d 7 7f 6f 3f 6 5b 4f 66 6d 7d 7 7f 6f 3f 6 5b 4f 66 6d 7d 7 7f 6f 3f 6 5b 4f 66 6d 7d 7
  //   7f 6f 3f 6 5b 4f 66 6d 7d 7 7f 6f 3f 6 5b 4f 66 6d 7d 7 7f 7 7d 6d 66 4f 5b 6 3f 6f 7f 7 7d 6d 66 4f
  //   5b 6 3f 6f 7f 7 7d 6d 66 4f 5b 6 3f 6f 7f 7 7d 6d 66 4f 5b 6 3f 6f 7f 7 7d 6d 66 4f 5b 6 3f 6f 7f 7
  //   7d 6d 66 4f 5b 6 3f 6f 7f 7 7d 6d 66 4f 5b 6 3f 6f 7f 7 7d 6d 66 4f 5b 6 3f 6f 7f 7 7d 6d 66 4f 5b 6
  //   3f 6f 7f 7 7d 6d 66 4f 5b 6 3f 6f 7f 7 7d 6d 66 4f 5b 6 3f 6f 7f 7 7d 6d 66 4f 5b 6 3f 6f 7f 7 7d 6d
  //   66 4f 5b 6
  //   contents of rom_2 (hex, n*v repeats v):
  //   10*3f 10*6 10*5b 10*4f 10*66 10*6d 10*7d 10*7 10*7f 10*6f 10*3f 10*6 17*5b 10*6 10*3f 10*6f 10*7f
  //   10*7 10*7d 10*6d 10*66 10*4f 10*5b 10*6 9*3f
  //   contents of rom_3 (hex, n*v repeats v):
  //   100*3f 57*6 99*3f
endmodule

module Binary_Keyboard (
  input  Input_Request,
  input  [7:0] Binary_keyboard_input,
  input  Enter_push_button,
  output halt,
  output Buffer_not_empty_indicator,
  output [7:0] Keyboard_Value
);

  wire d_ff_1_qn, not_1_out;

  not not_1 (not_1_out, Input_Request);
  Keyboard_Buffer_Register keyboard_buffer_register_1 (
    .\input (Binary_keyboard_input), .\output (Keyboard_Value), .clk(Enter_push_button), .write_enable(1'b1));
  and and_1 (halt, Input_Request, d_ff_1_qn);
  D_Flip_Flop d_ff_1 (
    .clk(not_1_out), .D(1'b0), .Q(Buffer_not_empty_indicator), .Qn(d_ff_1_qn), .preset(Enter_push_button));  // open: en, reset

  // Notes on the sheet:
  //   Buffer Indicator
  //   Memory Cell
endmodule

// Acc
module Acc__Accumulator (
  input  clk,
  input  write_enable,
  input  [7:0] \input ,
  output [7:0] \output 
);

  D_Flip_Flop d_ff_1 (.clk(clk), .D(\input [0]), .Q(\output [0]), .en(write_enable));  // open: Qn, preset, reset
  D_Flip_Flop d_ff_2 (.clk(clk), .D(\input [1]), .Q(\output [1]), .en(write_enable));  // open: Qn, preset, reset
  D_Flip_Flop d_ff_3 (.clk(clk), .D(\input [2]), .Q(\output [2]), .en(write_enable));  // open: Qn, preset, reset
  D_Flip_Flop d_ff_4 (.clk(clk), .D(\input [3]), .Q(\output [3]), .en(write_enable));  // open: Qn, preset, reset
  D_Flip_Flop d_ff_5 (.clk(clk), .D(\input [4]), .Q(\output [4]), .en(write_enable));  // open: Qn, preset, reset
  D_Flip_Flop d_ff_6 (.clk(clk), .D(\input [5]), .Q(\output [5]), .en(write_enable));  // open: Qn, preset, reset
  D_Flip_Flop d_ff_7 (.clk(clk), .D(\input [6]), .Q(\output [6]), .en(write_enable));  // open: Qn, preset, reset
  D_Flip_Flop d_ff_8 (.clk(clk), .D(\input [7]), .Q(\output [7]), .en(write_enable));  // open: Qn, preset, reset

  // Notes on the sheet:
  //   8 bits register
endmodule

// SP
module SP__Stack_Pointer_Register (
  input  clk,
  input  write_enable,
  input  [7:0] \input ,
  output [7:0] \output 
);

  D_Flip_Flop d_ff_1 (.clk(clk), .D(\input [0]), .Q(\output [0]), .en(write_enable));  // open: Qn, preset, reset
  D_Flip_Flop d_ff_2 (.clk(clk), .D(\input [1]), .Q(\output [1]), .en(write_enable));  // open: Qn, preset, reset
  D_Flip_Flop d_ff_3 (.clk(clk), .D(\input [2]), .Q(\output [2]), .en(write_enable));  // open: Qn, preset, reset
  D_Flip_Flop d_ff_4 (.clk(clk), .D(\input [3]), .Q(\output [3]), .en(write_enable));  // open: Qn, preset, reset
  D_Flip_Flop d_ff_5 (.clk(clk), .D(\input [4]), .Q(\output [4]), .en(write_enable));  // open: Qn, preset, reset
  D_Flip_Flop d_ff_6 (.clk(clk), .D(\input [5]), .Q(\output [5]), .en(write_enable));  // open: Qn, preset, reset
  D_Flip_Flop d_ff_7 (.clk(clk), .D(\input [6]), .Q(\output [6]), .en(write_enable));  // open: Qn, preset, reset
  D_Flip_Flop d_ff_8 (.clk(clk), .D(\input [7]), .Q(\output [7]), .en(write_enable));  // open: Qn, preset, reset

  // Notes on the sheet:
  //   8 bits register
endmodule

// PC
module PC__Program_Counter (
  input  clk,
  input  write_enable,
  input  [7:0] \input ,
  output [7:0] \output 
);

  D_Flip_Flop d_ff_1 (.clk(clk), .D(\input [0]), .Q(\output [0]), .en(write_enable));  // open: Qn, preset, reset
  D_Flip_Flop d_ff_2 (.clk(clk), .D(\input [1]), .Q(\output [1]), .en(write_enable));  // open: Qn, preset, reset
  D_Flip_Flop d_ff_3 (.clk(clk), .D(\input [2]), .Q(\output [2]), .en(write_enable));  // open: Qn, preset, reset
  D_Flip_Flop d_ff_4 (.clk(clk), .D(\input [3]), .Q(\output [3]), .en(write_enable));  // open: Qn, preset, reset
  D_Flip_Flop d_ff_5 (.clk(clk), .D(\input [4]), .Q(\output [4]), .en(write_enable));  // open: Qn, preset, reset
  D_Flip_Flop d_ff_6 (.clk(clk), .D(\input [5]), .Q(\output [5]), .en(write_enable));  // open: Qn, preset, reset
  D_Flip_Flop d_ff_7 (.clk(clk), .D(\input [6]), .Q(\output [6]), .en(write_enable));  // open: Qn, preset, reset
  D_Flip_Flop d_ff_8 (.clk(clk), .D(\input [7]), .Q(\output [7]), .en(write_enable));  // open: Qn, preset, reset

  // Notes on the sheet:
  //   8 bits register
endmodule

// IR
module IR__Instruction_Register (
  input  clk,
  input  write_enable,
  input  [7:0] \input ,
  output [7:0] \output 
);

  D_Flip_Flop d_ff_1 (.clk(clk), .D(\input [0]), .Q(\output [0]), .en(write_enable));  // open: Qn, preset, reset
  D_Flip_Flop d_ff_2 (.clk(clk), .D(\input [1]), .Q(\output [1]), .en(write_enable));  // open: Qn, preset, reset
  D_Flip_Flop d_ff_3 (.clk(clk), .D(\input [2]), .Q(\output [2]), .en(write_enable));  // open: Qn, preset, reset
  D_Flip_Flop d_ff_4 (.clk(clk), .D(\input [3]), .Q(\output [3]), .en(write_enable));  // open: Qn, preset, reset
  D_Flip_Flop d_ff_5 (.clk(clk), .D(\input [4]), .Q(\output [4]), .en(write_enable));  // open: Qn, preset, reset
  D_Flip_Flop d_ff_6 (.clk(clk), .D(\input [5]), .Q(\output [5]), .en(write_enable));  // open: Qn, preset, reset
  D_Flip_Flop d_ff_7 (.clk(clk), .D(\input [6]), .Q(\output [6]), .en(write_enable));  // open: Qn, preset, reset
  D_Flip_Flop d_ff_8 (.clk(clk), .D(\input [7]), .Q(\output [7]), .en(write_enable));  // open: Qn, preset, reset

  // Notes on the sheet:
  //   8 bits register
endmodule

// AB
module AB__Address_Bus (
  input  clk,
  input  write_enable,
  input  [7:0] \input ,
  output [7:0] \output 
);

  D_Flip_Flop d_ff_1 (.clk(clk), .D(\input [0]), .Q(\output [0]), .en(write_enable));  // open: Qn, preset, reset
  D_Flip_Flop d_ff_2 (.clk(clk), .D(\input [1]), .Q(\output [1]), .en(write_enable));  // open: Qn, preset, reset
  D_Flip_Flop d_ff_3 (.clk(clk), .D(\input [2]), .Q(\output [2]), .en(write_enable));  // open: Qn, preset, reset
  D_Flip_Flop d_ff_4 (.clk(clk), .D(\input [3]), .Q(\output [3]), .en(write_enable));  // open: Qn, preset, reset
  D_Flip_Flop d_ff_5 (.clk(clk), .D(\input [4]), .Q(\output [4]), .en(write_enable));  // open: Qn, preset, reset
  D_Flip_Flop d_ff_6 (.clk(clk), .D(\input [5]), .Q(\output [5]), .en(write_enable));  // open: Qn, preset, reset
  D_Flip_Flop d_ff_7 (.clk(clk), .D(\input [6]), .Q(\output [6]), .en(write_enable));  // open: Qn, preset, reset
  D_Flip_Flop d_ff_8 (.clk(clk), .D(\input [7]), .Q(\output [7]), .en(write_enable));  // open: Qn, preset, reset

  // Notes on the sheet:
  //   8 bits register
endmodule

// SC
module SC__Sequencer_Controller (
  input  [2:0] sequencer_commands,
  input  ZF,
  input  NF,
  output Mux1,
  output Mux0
);

  wire and_1_out, and_2_out, nor_1_out, xnor_1_out, xnor_2_out;

  xnor xnor_1 (xnor_1_out, sequencer_commands[0], ZF);
  xnor xnor_2 (xnor_2_out, sequencer_commands[0], NF);
  or or_1 (Mux1, sequencer_commands[2], ~sequencer_commands[1]);  // OR_Gate
  nor nor_1 (nor_1_out, sequencer_commands[2], sequencer_commands[0]);
  and and_1 (and_1_out, sequencer_commands[2], ~sequencer_commands[1], xnor_1_out);  // AND_Gate
  and and_2 (and_2_out, sequencer_commands[2], sequencer_commands[1], xnor_2_out);
  or or_2 (Mux0, nor_1_out, and_1_out, and_2_out);

  // Notes on the sheet:
  //   100 : jump if zero
  //   simple combinational circuit to
  //   implement sequencer commands
  //   001 : jump to the next address
  //   010 : get OPcode address
  //   011 : goto fetch address
  //   101 : jump if not zero
  //   110 : jump if negative
  //   111 : jump if not negative
  //   Sequencer Controller commands
  //   000 : increment to the next address
endmodule

// MPC
module MPC__Micro_instruction_Program_Counter (
  input  clk,
  input  write_enable,
  input  [7:0] \input ,
  output [7:0] \output 
);

  D_Flip_Flop d_ff_1 (.clk(clk), .D(\input [0]), .Q(\output [0]), .en(write_enable));  // open: Qn, preset, reset
  D_Flip_Flop d_ff_2 (.clk(clk), .D(\input [1]), .Q(\output [1]), .en(write_enable));  // open: Qn, preset, reset
  D_Flip_Flop d_ff_3 (.clk(clk), .D(\input [2]), .Q(\output [2]), .en(write_enable));  // open: Qn, preset, reset
  D_Flip_Flop d_ff_4 (.clk(clk), .D(\input [3]), .Q(\output [3]), .en(write_enable));  // open: Qn, preset, reset
  D_Flip_Flop d_ff_5 (.clk(clk), .D(\input [4]), .Q(\output [4]), .en(write_enable));  // open: Qn, preset, reset
  D_Flip_Flop d_ff_6 (.clk(clk), .D(\input [5]), .Q(\output [5]), .en(write_enable));  // open: Qn, preset, reset
  D_Flip_Flop d_ff_7 (.clk(clk), .D(\input [6]), .Q(\output [6]), .en(write_enable));  // open: Qn, preset, reset
  D_Flip_Flop d_ff_8 (.clk(clk), .D(\input [7]), .Q(\output [7]), .en(write_enable));  // open: Qn, preset, reset

  // Notes on the sheet:
  //   8 bits register
endmodule

// CSR
module CSR__Control_Signals_Register (
  input  clk,
  input  write_enable,
  input  [23:0] \input ,
  output J7,
  output J6,
  output J5,
  output J4,
  output J3,
  output J2,
  output J1,
  output J0,
  output SC2,
  output SC1,
  output SC0,
  output IR,
  output OW,
  output MWR_,
  output M1,
  output M0,
  output F2,
  output F1,
  output F0,
  output ABw,
  output IRw,
  output PCw,
  output SPw,
  output Accw
);

  D_Flip_Flop d_ff_1 (.clk(clk), .D(\input [0]), .Q(Accw), .en(write_enable));  // open: Qn, preset, reset
  D_Flip_Flop d_ff_2 (.clk(clk), .D(\input [1]), .Q(SPw), .en(write_enable));  // open: Qn, preset, reset
  D_Flip_Flop d_ff_3 (.clk(clk), .D(\input [2]), .Q(PCw), .en(write_enable));  // open: Qn, preset, reset
  D_Flip_Flop d_ff_4 (.clk(clk), .D(\input [3]), .Q(IRw), .en(write_enable));  // open: Qn, preset, reset
  D_Flip_Flop d_ff_5 (.clk(clk), .D(\input [4]), .Q(ABw), .en(write_enable));  // open: Qn, preset, reset
  D_Flip_Flop d_ff_6 (.clk(clk), .D(\input [5]), .Q(F0), .en(write_enable));  // open: Qn, preset, reset
  D_Flip_Flop d_ff_7 (.clk(clk), .D(\input [6]), .Q(F1), .en(write_enable));  // open: Qn, preset, reset
  D_Flip_Flop d_ff_8 (.clk(clk), .D(\input [7]), .Q(F2), .en(write_enable));  // open: Qn, preset, reset
  D_Flip_Flop d_ff_9 (.clk(clk), .D(\input [8]), .Q(M0), .en(write_enable));  // open: Qn, preset, reset
  D_Flip_Flop d_ff_10 (.clk(clk), .D(\input [9]), .Q(M1), .en(write_enable));  // open: Qn, preset, reset
  D_Flip_Flop d_ff_11 (.clk(clk), .D(\input [10]), .Q(MWR_), .en(write_enable));  // open: Qn, preset, reset
  D_Flip_Flop d_ff_12 (.clk(clk), .D(\input [11]), .Q(OW), .en(write_enable));  // open: Qn, preset, reset
  D_Flip_Flop d_ff_13 (.clk(clk), .D(\input [12]), .Q(IR), .en(write_enable));  // open: Qn, preset, reset
  D_Flip_Flop d_ff_14 (.clk(clk), .D(\input [13]), .Q(SC0), .en(write_enable));  // open: Qn, preset, reset
  D_Flip_Flop d_ff_15 (.clk(clk), .D(\input [14]), .Q(SC1), .en(write_enable));  // open: Qn, preset, reset
  D_Flip_Flop d_ff_16 (.clk(clk), .D(\input [15]), .Q(SC2), .en(write_enable));  // open: Qn, preset, reset
  D_Flip_Flop d_ff_17 (.clk(clk), .D(\input [16]), .Q(J0), .en(write_enable));  // open: Qn, preset, reset
  D_Flip_Flop d_ff_18 (.clk(clk), .D(\input [17]), .Q(J1), .en(write_enable));  // open: Qn, preset, reset
  D_Flip_Flop d_ff_19 (.clk(clk), .D(\input [18]), .Q(J2), .en(write_enable));  // open: Qn, preset, reset
  D_Flip_Flop d_ff_20 (.clk(clk), .D(\input [19]), .Q(J3), .en(write_enable));  // open: Qn, preset, reset
  D_Flip_Flop d_ff_21 (.clk(clk), .D(\input [20]), .Q(J4), .en(write_enable));  // open: Qn, preset, reset
  D_Flip_Flop d_ff_22 (.clk(clk), .D(\input [21]), .Q(J5), .en(write_enable));  // open: Qn, preset, reset
  D_Flip_Flop d_ff_23 (.clk(clk), .D(\input [22]), .Q(J6), .en(write_enable));  // open: Qn, preset, reset
  D_Flip_Flop d_ff_24 (.clk(clk), .D(\input [23]), .Q(J7), .en(write_enable));  // open: Qn, preset, reset

  // Notes on the sheet:
  //   24 bits register
endmodule

module Output_Register (
  input  clk,
  input  write_enable,
  input  [7:0] \input ,
  output [7:0] \output 
);

  D_Flip_Flop d_ff_1 (.clk(clk), .D(\input [0]), .Q(\output [0]), .en(write_enable));  // open: Qn, preset, reset
  D_Flip_Flop d_ff_2 (.clk(clk), .D(\input [1]), .Q(\output [1]), .en(write_enable));  // open: Qn, preset, reset
  D_Flip_Flop d_ff_3 (.clk(clk), .D(\input [2]), .Q(\output [2]), .en(write_enable));  // open: Qn, preset, reset
  D_Flip_Flop d_ff_4 (.clk(clk), .D(\input [3]), .Q(\output [3]), .en(write_enable));  // open: Qn, preset, reset
  D_Flip_Flop d_ff_5 (.clk(clk), .D(\input [4]), .Q(\output [4]), .en(write_enable));  // open: Qn, preset, reset
  D_Flip_Flop d_ff_6 (.clk(clk), .D(\input [5]), .Q(\output [5]), .en(write_enable));  // open: Qn, preset, reset
  D_Flip_Flop d_ff_7 (.clk(clk), .D(\input [6]), .Q(\output [6]), .en(write_enable));  // open: Qn, preset, reset
  D_Flip_Flop d_ff_8 (.clk(clk), .D(\input [7]), .Q(\output [7]), .en(write_enable));  // open: Qn, preset, reset

  // Notes on the sheet:
  //   8 bits register
endmodule

// KB Buffer
module Keyboard_Buffer_Register (
  input  clk,
  input  write_enable,
  input  [7:0] \input ,
  output [7:0] \output 
);

  D_Flip_Flop d_ff_1 (.clk(clk), .D(\input [0]), .Q(\output [0]), .en(write_enable));  // open: Qn, preset, reset
  D_Flip_Flop d_ff_2 (.clk(clk), .D(\input [1]), .Q(\output [1]), .en(write_enable));  // open: Qn, preset, reset
  D_Flip_Flop d_ff_3 (.clk(clk), .D(\input [2]), .Q(\output [2]), .en(write_enable));  // open: Qn, preset, reset
  D_Flip_Flop d_ff_4 (.clk(clk), .D(\input [3]), .Q(\output [3]), .en(write_enable));  // open: Qn, preset, reset
  D_Flip_Flop d_ff_5 (.clk(clk), .D(\input [4]), .Q(\output [4]), .en(write_enable));  // open: Qn, preset, reset
  D_Flip_Flop d_ff_6 (.clk(clk), .D(\input [5]), .Q(\output [5]), .en(write_enable));  // open: Qn, preset, reset
  D_Flip_Flop d_ff_7 (.clk(clk), .D(\input [6]), .Q(\output [6]), .en(write_enable));  // open: Qn, preset, reset
  D_Flip_Flop d_ff_8 (.clk(clk), .D(\input [7]), .Q(\output [7]), .en(write_enable));  // open: Qn, preset, reset

  // Notes on the sheet:
  //   8 bits register
endmodule

// Mux 4-1
module Mux_4_1__8_bits (
  input  Select_1,
  input  Select_0,
  input  [7:0] Input_0,
  input  [7:0] Input_1,
  input  [7:0] Input_2,
  input  [7:0] Input_3,
  output [7:0] Output
);

  wire [7:0] and_1_out, and_2_out, and_3_out, and_4_out, not_1_out, not_2_out;

  assign not_1_out = ~{8{Select_1}};  // NOT_Gate not_1, 8 bits wide
  assign not_2_out = ~{8{Select_0}};  // NOT_Gate not_2, 8 bits wide
  assign and_1_out = not_2_out & not_1_out & Input_0;  // AND_Gate and_1, 8 bits wide
  assign and_2_out = {8{Select_0}} & not_1_out & Input_1;  // AND_Gate and_2, 8 bits wide
  assign and_3_out = not_2_out & {8{Select_1}} & Input_2;  // AND_Gate and_3, 8 bits wide
  assign and_4_out = {8{Select_0}} & {8{Select_1}} & Input_3;  // AND_Gate and_4, 8 bits wide
  assign Output = and_1_out | and_2_out | and_3_out | and_4_out;  // OR_Gate or_1, 8 bits wide
endmodule

// Mux 8-1
module Mux_8_1__8_bits (
  input  Select_2,
  input  Select_1,
  input  Select_0,
  input  [7:0] Input_0,
  input  [7:0] Input_1,
  input  [7:0] Input_2,
  input  [7:0] Input_3,
  input  [7:0] Input_4,
  input  [7:0] Input_5,
  input  [7:0] Input_6,
  input  [7:0] Input_7,
  output [7:0] Output
);

  wire [7:0] and_1_out, and_2_out, and_3_out, and_4_out, and_5_out, and_6_out, and_7_out, and_8_out,
       not_1_out, not_2_out, not_3_out;

  assign not_1_out = ~{8{Select_2}};  // NOT_Gate not_1, 8 bits wide
  assign not_2_out = ~{8{Select_1}};  // NOT_Gate not_2, 8 bits wide
  assign not_3_out = ~{8{Select_0}};  // NOT_Gate not_3, 8 bits wide
  assign and_1_out = not_3_out & not_2_out & not_1_out & Input_0;  // AND_Gate and_1, 8 bits wide
  assign and_2_out = {8{Select_0}} & not_2_out & not_1_out & Input_1;  // AND_Gate and_2, 8 bits wide
  assign and_3_out = not_3_out & {8{Select_1}} & not_1_out & Input_2;  // AND_Gate and_3, 8 bits wide
  assign and_4_out = {8{Select_0}} & {8{Select_1}} & not_1_out & Input_3;  // AND_Gate and_4, 8 bits wide
  assign and_5_out = not_3_out & not_2_out & {8{Select_2}} & Input_4;  // AND_Gate and_5, 8 bits wide
  assign and_6_out = {8{Select_0}} & not_2_out & {8{Select_2}} & Input_5;  // AND_Gate and_6, 8 bits wide
  assign and_7_out = not_3_out & {8{Select_1}} & {8{Select_2}} & Input_6;  // AND_Gate and_7, 8 bits wide
  assign and_8_out = {8{Select_0}} & {8{Select_1}} & {8{Select_2}} & Input_7;  // AND_Gate and_8, 8 bits wide
  assign Output = and_1_out | and_2_out | and_3_out | and_4_out | and_5_out | and_6_out | and_7_out | and_8_out;  // OR_Gate or_1, 8 bits wide
endmodule

module Full_Adder (
  input  Cin,
  input  A,
  input  B,
  output S,
  output Cout
);

  wire and_1_out, and_2_out, and_3_out;

  xor xor_1 (S, A, B, Cin);
  and and_1 (and_1_out, A, B);
  and and_2 (and_2_out, A, Cin);
  and and_3 (and_3_out, B, Cin);
  or or_1 (Cout, and_1_out, and_2_out, and_3_out);
endmodule

// +
module Adder__8_bits (
  input  [7:0] A,
  input  [7:0] B,
  output [7:0] S,
  output Cout
);

  wire full_adder_1_cout, full_adder_2_cout, full_adder_3_cout, full_adder_4_cout, full_adder_5_cout,
       full_adder_6_cout, full_adder_7_cout;

  Full_Adder full_adder_1 (.A(A[0]), .B(B[0]), .S(S[0]), .Cin(1'b0), .Cout(full_adder_1_cout));
  Full_Adder full_adder_2 (.A(A[1]), .B(B[1]), .S(S[1]), .Cin(full_adder_1_cout), .Cout(full_adder_2_cout));
  Full_Adder full_adder_3 (.A(A[2]), .B(B[2]), .S(S[2]), .Cin(full_adder_2_cout), .Cout(full_adder_3_cout));
  Full_Adder full_adder_4 (.A(A[3]), .B(B[3]), .S(S[3]), .Cin(full_adder_3_cout), .Cout(full_adder_4_cout));
  Full_Adder full_adder_5 (.A(A[4]), .B(B[4]), .S(S[4]), .Cin(full_adder_4_cout), .Cout(full_adder_5_cout));
  Full_Adder full_adder_6 (.A(A[5]), .B(B[5]), .S(S[5]), .Cin(full_adder_5_cout), .Cout(full_adder_6_cout));
  Full_Adder full_adder_7 (.A(A[6]), .B(B[6]), .S(S[6]), .Cin(full_adder_6_cout), .Cout(full_adder_7_cout));
  Full_Adder full_adder_8 (.A(A[7]), .B(B[7]), .S(S[7]), .Cin(full_adder_7_cout), .Cout(Cout));
endmodule

// -
module Subtractor__8_bits (
  input  [7:0] A,
  input  [7:0] B,
  output [7:0] S,
  output Cout
);

  wire full_adder_1_cout, full_adder_2_cout, full_adder_3_cout, full_adder_4_cout, full_adder_5_cout,
       full_adder_6_cout, full_adder_7_cout;
  wire [7:0] not_1_out;

  assign not_1_out = ~B;  // NOT_Gate not_1, 8 bits wide
  Full_Adder full_adder_1 (.A(A[0]), .B(not_1_out[0]), .S(S[0]), .Cin(1'b1), .Cout(full_adder_1_cout));
  Full_Adder full_adder_2 (.A(A[1]), .B(not_1_out[1]), .S(S[1]), .Cin(full_adder_1_cout), .Cout(full_adder_2_cout));
  Full_Adder full_adder_3 (.A(A[2]), .B(not_1_out[2]), .S(S[2]), .Cin(full_adder_2_cout), .Cout(full_adder_3_cout));
  Full_Adder full_adder_4 (.A(A[3]), .B(not_1_out[3]), .S(S[3]), .Cin(full_adder_3_cout), .Cout(full_adder_4_cout));
  Full_Adder full_adder_5 (.A(A[4]), .B(not_1_out[4]), .S(S[4]), .Cin(full_adder_4_cout), .Cout(full_adder_5_cout));
  Full_Adder full_adder_6 (.A(A[5]), .B(not_1_out[5]), .S(S[5]), .Cin(full_adder_5_cout), .Cout(full_adder_6_cout));
  Full_Adder full_adder_7 (.A(A[6]), .B(not_1_out[6]), .S(S[6]), .Cin(full_adder_6_cout), .Cout(full_adder_7_cout));
  Full_Adder full_adder_8 (.A(A[7]), .B(not_1_out[7]), .S(S[7]), .Cin(full_adder_7_cout), .Cout(Cout));
endmodule

// +1
module Incrementation__8_bits (
  input  [7:0] A,
  output [7:0] S
);

  Adder__8_bits adder_8_bits_1 (.A(A), .B(8'h1), .S(S));  // open: Cout
endmodule

// -1
module Decrementation__8_bits (
  input  [7:0] A,
  output [7:0] S
);

  Subtractor__8_bits subtractor_8_bits_1 (.A(A), .B(8'h1), .S(S));  // open: Cout
endmodule

module Shift_Right (
  input  [7:0] A,
  output [7:0] S
);


  assign S = {1'b0, A[7:1]};
endmodule
